// Logisim project Pipelined_CPU.circ as structural Verilog: 10 circuits, main circuit New_main
module _16_bit_register_file (
  input  Reset,
  input  [2:0] Read_Reg_1,
  input  [2:0] Read_Reg_2,
  input  Write,
  input  [2:0] Write_Reg_Destination,
  input  [15:0] Write_Data,
  output [15:0] Read_Reg_1_Output,
  output [15:0] Read_Reg_2_Output
);

  wire demultiplexer_1_out0, demultiplexer_1_out1, demultiplexer_1_out2, demultiplexer_1_out3,
       demultiplexer_1_out4, demultiplexer_1_out5, demultiplexer_1_out6, demultiplexer_1_out7;
  wire [15:0] r0_q, r1_q, r2_q, r3_q, r4_q, r5_q, r6_q;

  Demultiplexer #(.select(3)) demultiplexer_1 (
    .out0(demultiplexer_1_out0), .out1(demultiplexer_1_out1), .out2(demultiplexer_1_out2),
    .out3(demultiplexer_1_out3), .out4(demultiplexer_1_out4), .out5(demultiplexer_1_out5),
    .out6(demultiplexer_1_out6), .out7(demultiplexer_1_out7), .in(Write), .sel(Write_Reg_Destination));  // open: en
  Register #(.width(16)) r0 (.D(Write_Data), .Q(r0_q), .clk(demultiplexer_1_out0), .clr(Reset));  // open: en
  Register #(.width(16)) r1 (.D(Write_Data), .Q(r1_q), .clk(demultiplexer_1_out1), .clr(Reset));  // open: en
  Register #(.width(16)) r2 (.D(Write_Data), .Q(r2_q), .clk(demultiplexer_1_out2), .clr(Reset));  // open: en
  Register #(.width(16)) r3 (.D(Write_Data), .Q(r3_q), .clk(demultiplexer_1_out3), .clr(Reset));  // open: en
  Register #(.width(16)) r4 (.D(Write_Data), .Q(r4_q), .clk(demultiplexer_1_out4), .clr(Reset));  // open: en
  Register #(.width(16)) r5 (.D(Write_Data), .Q(r5_q), .clk(demultiplexer_1_out5), .clr(Reset));  // open: en
  Register #(.width(16)) r6 (.D(Write_Data), .Q(r6_q), .clk(demultiplexer_1_out6), .clr(Reset));  // open: en
  Register #(.width(16)) r7 (.D(Write_Data), .Q(r3_q), .clk(demultiplexer_1_out7), .clr(Reset));  // open: en
  Multiplexer #(.select(3), .width(16), .enable("false")) multiplexer_1 (
    .in0(r0_q), .in1(r1_q), .in2(r2_q), .in3(r3_q), .in4(r4_q), .in5(r5_q), .in6(r6_q), .in7(r3_q),
    .out(Read_Reg_1_Output), .sel(Read_Reg_1));
  Multiplexer #(.select(3), .width(16), .enable("false")) multiplexer_2 (
    .in0(r0_q), .in1(r1_q), .in2(r2_q), .in3(r3_q), .in4(r4_q), .in5(r5_q), .in6(r6_q), .in7(r3_q),
    .out(Read_Reg_2_Output), .sel(Read_Reg_2));
endmodule

module Instruction_Memory (
  input  [7:0] Address,
  output [15:0] Output
);

  ROM #(.dataWidth(16)) rom_1 (.addr(Address), .data(Output), .sel(1'b1));
endmodule

module Data_Memory (
  input  [7:0] Address,
  input  [15:0] Data_In,
  output [15:0] Data_Out
);

  RAM #(.dataWidth(16), .bus("separate")) ram_1 (
    .addr(Address), .din(Data_In), .data(Data_Out), .sel(1'b1));  // open: str, clk, ld, clr
endmodule

module ALU (
  input  [15:0] Input_A,
  input  [15:0] Input_B,
  output [15:0] ALU_Output
);

  wire [15:0] adder_1_out, comparator_1_eq, comparator_1_gt, comparator_1_lt;

  Adder #(.width(16)) adder_1 (.a(Input_A), .b(Input_B), .out(adder_1_out));  // open: cin, cout
  Subtractor #(.width(16)) subtractor_1 (.a(Input_A), .b(Input_B), .out(adder_1_out));  // open: bin, bout
  Comparator #(.width(16)) comparator_1 (
    .a(Input_A), .b(Input_B), .gt(comparator_1_gt[0]), .eq(comparator_1_eq[0]), .lt(comparator_1_lt[0]));
  Multiplexer #(.select(3), .width(16)) multiplexer_1 (
    .in0(adder_1_out), .in1(adder_1_out), .in2(comparator_1_gt), .in3(comparator_1_eq),
    .in4(comparator_1_lt), .out(ALU_Output));  // open: in5, in6, in7, sel, en
  // Pins of 1 and 16 bits meet at comparator_1_gt
  // Pins of 1 and 16 bits meet at comparator_1_eq
  // Pins of 1 and 16 bits meet at comparator_1_lt
endmodule

module Sign_Extender (
  input  Unsigned,
  input  [7:0] Immediate,
  output [15:0] SignExtendedImm
);

  wire [15:0] bit_extender_1_out, bit_extender_2_out;

  assign bit_extender_1_out = {{8{Immediate[7]}}, Immediate};  // Bit_Extender bit_extender_1
  assign bit_extender_2_out = {{8{1'b0}}, Immediate};  // Bit_Extender bit_extender_2
  Multiplexer #(.width(16), .disabled(0), .enable("false")) multiplexer_1 (
    .in0(bit_extender_1_out), .in1(bit_extender_2_out), .out(SignExtendedImm), .sel(Unsigned));
endmodule

module New_main (
);

  wire button_1_out, clock_1_out, Decoder_p1, Decoder_p2, Decoder_p3, Decoder_p5, Decoder_p6, Decoder_p7,
       Decoder_p8, ex_mem_buffer_1_read_data_1_4, ex_mem_buffer_1_read_data_1_6,
       ex_mem_buffer_1_read_data_1_8, ex_mem_buffer_1_read_data_1_11, ex_mem_buffer_1_read_data_1_12,
       ex_mem_buffer_1_read_data_1_13, ex_mem_buffer_1_read_data_1_14, ex_mem_buffer_1_read_data_1_15,
       ex_mem_buffer_1_read_data_1_16, ex_mem_buffer_1_read_data_1_17, id_ex_buffer_1_immtoalu_2,
       id_ex_buffer_1_immtopc_2, id_ex_buffer_1_led_2, id_ex_buffer_1_mem_to_reg_2, id_ex_buffer_1_memread_2,
       id_ex_buffer_1_memwrite_2, id_ex_buffer_1_pc_to_reg_2, id_ex_buffer_1_reg_to_pc_2,
       id_ex_buffer_1_shifter_to_reg_2, id_ex_buffer_1_shiftsource_2, id_ex_buffer_1_subop_2,
       id_ex_buffer_1_write_led_2, id_ex_buffer_1_zeros_to_alu_2, Instruction_Splitter_p2,
       Instruction_Splitter_p3, Instruction_Splitter_p4, Instruction_Splitter_p5, Instruction_Splitter_p7,
       Instruction_Splitter_p8, mem_wb_buffer_1_out_10, mem_wb_buffer_1_out_12, mem_wb_buffer_1_out_13,
       not_1_out, ResultToLess_p2, ResultToLess_p5, ResultToLess_p7, ResultToLess_p8, ResultToLess_p9,
       ResultToLess_p10, ResultToLess_p11, ResultToLess_p12, ResultToLess_p13;
  wire [3:0] Decoder_p4, ex_mem_buffer_1_read_data_1_9, id_ex_buffer_1_alu_op_2,
       id_ex_buffer_1_shiftamount_2, Instruction_Splitter_p6;
  wire [7:0] adder_1_out, ex_mem_buffer_1_out_21, ex_mem_buffer_1_read_data_1,
       ex_mem_buffer_1_read_data_1_10, id_ex_buffer_1_immediate_2, id_ex_buffer_1_pc_plus_4_3,
       id_ex_buffer_1_pc_plus_4_4, Instruction_Splitter_p9, multiplexer_3_out, multiplexer_4_out, PC_q,
       RegistertoAddress_2_p2, RegistertoAddress_p2;
  wire [15:0] ALU_p5, bit_extender_1_out, ex_mem_buffer_1_read_data_1_3, ex_mem_buffer_1_read_data_1_5,
       ex_mem_buffer_1_read_data_1_7, id_ex_buffer_1_read_data_1_3, id_ex_buffer_1_read_data_1_4,
       id_ex_buffer_1_read_data_2_4, id_ex_buffer_1_read_data_2_5, id_ex_buffer_1_read_data_2_6,
       id_ex_buffer_1_sign_extended_immediate_2, IF_ID_Buffer_data_out, mem_wb_buffer_1_out_8,
       mem_wb_buffer_1_out_9, mem_wb_buffer_1_out_11, multiplexer_1_out, multiplexer_2_out,
       multiplexer_6_out, multiplexer_7_out, ram_1_data, register_1_q, Registers_p4, Registers_p7,
       Registers_p8, ResultToLess_p1, rom_1_data, Shifter_p6, Sign_Extend_p3;

  not not_1 (not_1_out, ResultToLess_p9);
  Clock clock_1 (.out(clock_1_out));
  Register PC (.D(multiplexer_4_out), .en(not_1_out), .Q(PC_q), .clk(clock_1_out), .clr(button_1_out));
  Button button_1 (.out(button_1_out));
  Adder adder_1 (.a(PC_q), .b(8'h1), .out(adder_1_out));  // open: cin, cout
  ROM #(.dataWidth(16)) rom_1 (.addr(PC_q), .data(rom_1_data), .sel(1'b1));
  IF_ID_Buffer IF_ID_Buffer (
    .Data_in(rom_1_data), .ClockIn(clock_1_out), .EN(not_1_out), .Data_out(IF_ID_Buffer_data_out));
  // InstructionSplitter Instruction_Splitter: pin names not known; wires that end beside it: IF_ID_Buffer_data_out, Instruction_Splitter_p2, Instruction_Splitter_p3, Instruction_Splitter_p4, Instruction_Splitter_p5, Instruction_Splitter_p6, Instruction_Splitter_p7, Instruction_Splitter_p8, Instruction_Splitter_p9
  // ResultToLess ResultToLess: pin names not known; wires that end beside it: ResultToLess_p1, ResultToLess_p2, Instruction_Splitter_p2, Instruction_Splitter_p7, ResultToLess_p5, ResultToLess_p2, ResultToLess_p7, ResultToLess_p8, ResultToLess_p9, ResultToLess_p10, ResultToLess_p11, ResultToLess_p12, ResultToLess_p13
  // SignExtend Sign_Extend: pin names not known; wires that end beside it: Instruction_Splitter_p8, Instruction_Splitter_p9, Sign_Extend_p3
  // Decoder Decoder: pin names not known; wires that end beside it: Decoder_p1, Decoder_p2, Decoder_p3, Decoder_p4, Decoder_p5, Decoder_p6, Decoder_p7, Decoder_p8
  // RegisterFile Registers: pin names not known; wires that end beside it: Instruction_Splitter_p3, Instruction_Splitter_p4, Instruction_Splitter_p5, Registers_p4, Decoder_p3, clock_1_out, Registers_p7, Registers_p8
  ID_EX_Buffer id_ex_buffer_1 (
    .PC_plus_4(adder_1_out), .CLK(clock_1_out), .Immediate(Instruction_Splitter_p9),
    .Read_Data_1(Registers_p7), .Read_Data_2(Registers_p8), .Read_Data_2_2(Registers_p8),
    .Sign_Extended_Immediate(Sign_Extend_p3), .SubOP(Instruction_Splitter_p7), .Read_Data_1_2(Registers_p7),
    .Read_Data_2_3(Registers_p8), .ShiftSource(Decoder_p1), .ShiftAmount(Instruction_Splitter_p6),
    .PC_Plus_4_2(adder_1_out), .Shifter_to_reg(Decoder_p2), .ALU_op(Decoder_p4), .IMMtoALU(Decoder_p5),
    .Reg_to_PC(Decoder_p6), .IMMtoPC(Decoder_p7), .Zeros_to_ALU(Decoder_p8), .MemWrite(ResultToLess_p7),
    .Mem_to_Reg(ResultToLess_p8), .LED(ResultToLess_p10), .Write_LED(ResultToLess_p11),
    .MemRead(ResultToLess_p12), .PC_to_Reg(ResultToLess_p13), .PC_plus_4_3(id_ex_buffer_1_pc_plus_4_3),
    .Immediate_2(id_ex_buffer_1_immediate_2), .Read_Data_1_3(id_ex_buffer_1_read_data_1_3),
    .Read_Data_2_4(id_ex_buffer_1_read_data_2_4), .Read_Data_2_5(id_ex_buffer_1_read_data_2_5),
    .Sign_Extended_Immediate_2(id_ex_buffer_1_sign_extended_immediate_2), .SubOp_2(id_ex_buffer_1_subop_2),
    .Read_Data_1_4(id_ex_buffer_1_read_data_1_4), .Read_Data_2_6(id_ex_buffer_1_read_data_2_6),
    .ShiftSource_2(id_ex_buffer_1_shiftsource_2), .ShiftAmount_2(id_ex_buffer_1_shiftamount_2),
    .PC_Plus_4_4(id_ex_buffer_1_pc_plus_4_4), .Shifter_to_reg_2(id_ex_buffer_1_shifter_to_reg_2),
    .ALU_op_2(id_ex_buffer_1_alu_op_2), .IMMtoALU_2(id_ex_buffer_1_immtoalu_2),
    .Reg_to_PC_2(id_ex_buffer_1_reg_to_pc_2), .IMMtoPC_2(id_ex_buffer_1_immtopc_2),
    .Zeros_to_ALU_2(id_ex_buffer_1_zeros_to_alu_2), .MemWrite_2(id_ex_buffer_1_memwrite_2),
    .Mem_to_Reg_2(id_ex_buffer_1_mem_to_reg_2), .LED_2(id_ex_buffer_1_led_2),
    .Write_LED_2(id_ex_buffer_1_write_led_2), .MemRead_2(id_ex_buffer_1_memread_2),
    .PC_to_Reg_2(id_ex_buffer_1_pc_to_reg_2));
  Multiplexer #(.width(16), .disabled(0), .enable("false")) multiplexer_1 (
    .in0(id_ex_buffer_1_read_data_2_4), .in1(id_ex_buffer_1_sign_extended_immediate_2),
    .out(multiplexer_1_out), .sel(id_ex_buffer_1_immtoalu_2));
  // ALUtoPC RegistertoAddress: pin names not known; wires that end beside it: id_ex_buffer_1_read_data_1_3, RegistertoAddress_p2
  Multiplexer #(.width(16), .disabled(0), .enable("false")) multiplexer_2 (
    .in0(multiplexer_1_out), .in1({16{1'b0}}), .out(multiplexer_2_out), .sel(id_ex_buffer_1_zeros_to_alu_2));
  Multiplexer #(.width(8), .disabled(0), .enable("false")) multiplexer_3 (
    .in0(id_ex_buffer_1_pc_plus_4_3), .in1(id_ex_buffer_1_immediate_2), .out(multiplexer_3_out),
    .sel(id_ex_buffer_1_immtopc_2));
  // sixteen_bit_ALU ALU: pin names not known; wires that end beside it: id_ex_buffer_1_alu_op_2, id_ex_buffer_1_read_data_1_3, multiplexer_2_out, ResultToLess_p5, ALU_p5
  EX_MEM_Buffer ex_mem_buffer_1 (
    .CLK(clock_1_out), .in_2(multiplexer_3_out), .in_3(RegistertoAddress_p2), .in_4(ALU_p5),
    .in_5(id_ex_buffer_1_read_data_2_5), .in_6(id_ex_buffer_1_shifter_to_reg_2),
    .in_7(id_ex_buffer_1_read_data_1_4), .in_8(id_ex_buffer_1_subop_2), .in_9(id_ex_buffer_1_read_data_2_6),
    .in_10(id_ex_buffer_1_shiftsource_2), .in_11(id_ex_buffer_1_shiftamount_2),
    .in_12(id_ex_buffer_1_pc_plus_4_4), .in_13(id_ex_buffer_1_reg_to_pc_2),
    .in_14(id_ex_buffer_1_memwrite_2), .in_15(id_ex_buffer_1_mem_to_reg_2), .in_16(id_ex_buffer_1_led_2),
    .in_17(id_ex_buffer_1_write_led_2), .in_18(id_ex_buffer_1_memread_2), .in_19(id_ex_buffer_1_pc_to_reg_2),
    .out_21(ex_mem_buffer_1_out_21), .Read_Data_1(ex_mem_buffer_1_read_data_1),
    .Read_Data_1_2(ResultToLess_p1), .Read_Data_1_3(ex_mem_buffer_1_read_data_1_3),
    .Read_Data_1_4(ex_mem_buffer_1_read_data_1_4), .Read_Data_1_5(ex_mem_buffer_1_read_data_1_5),
    .Read_Data_1_6(ex_mem_buffer_1_read_data_1_6), .Read_Data_1_7(ex_mem_buffer_1_read_data_1_7),
    .Read_Data_1_8(ex_mem_buffer_1_read_data_1_8), .Read_Data_1_9(ex_mem_buffer_1_read_data_1_9),
    .Read_Data_1_10(ex_mem_buffer_1_read_data_1_10), .Read_Data_1_11(ex_mem_buffer_1_read_data_1_11),
    .Read_Data_1_12(ex_mem_buffer_1_read_data_1_12), .Read_Data_1_13(ex_mem_buffer_1_read_data_1_13),
    .Read_Data_1_14(ex_mem_buffer_1_read_data_1_14), .Read_Data_1_15(ex_mem_buffer_1_read_data_1_15),
    .Read_Data_1_16(ex_mem_buffer_1_read_data_1_16), .Read_Data_1_17(ex_mem_buffer_1_read_data_1_17));  // open: in_20, Read_Data_1_18
  Multiplexer #(.width(8), .disabled(0), .enable("false")) multiplexer_4 (
    .in0(ex_mem_buffer_1_out_21), .in1(ex_mem_buffer_1_read_data_1), .out(multiplexer_4_out),
    .sel(ex_mem_buffer_1_read_data_1_11));
  // ALUtoPC RegistertoAddress_2: pin names not known; wires that end beside it: ex_mem_buffer_1_read_data_1_3, RegistertoAddress_2_p2
  Multiplexer #(.width(16), .disabled(0), .enable("false")) multiplexer_5 (
    .in0(multiplexer_6_out), .in1(bit_extender_1_out), .out(Registers_p4),
    .sel(ex_mem_buffer_1_read_data_1_16));
  // Shifter Shifter: pin names not known; wires that end beside it: ex_mem_buffer_1_read_data_1_6, ex_mem_buffer_1_read_data_1_5, ex_mem_buffer_1_read_data_1_7, ex_mem_buffer_1_read_data_1_8, ex_mem_buffer_1_read_data_1_9, Shifter_p6
  assign bit_extender_1_out = {{8{1'b0}}, ex_mem_buffer_1_read_data_1_10};  // Bit_Extender bit_extender_1
  Multiplexer #(.width(16), .disabled(0), .enable("false")) multiplexer_6 (
    .in0(multiplexer_7_out), .in1(Shifter_p6), .out(multiplexer_6_out), .sel(ex_mem_buffer_1_read_data_1_4));
  RAM #(.dataWidth(16), .bus("separate")) ram_1 (
    .addr(RegistertoAddress_2_p2), .din(ex_mem_buffer_1_read_data_1_5), .data(ram_1_data),
    .str(ex_mem_buffer_1_read_data_1_12), .sel(1'b1), .clk(clock_1_out), .ld(ex_mem_buffer_1_read_data_1_17));  // open: clr
  MEM_WB_Buffer mem_wb_buffer_1 (
    .CLK(clock_1_out), .in_2(ResultToLess_p1), .in_3(ram_1_data), .in_4(ex_mem_buffer_1_read_data_1_13),
    .in_5(ex_mem_buffer_1_read_data_1_5), .in_6(ex_mem_buffer_1_read_data_1_15),
    .in_7(ex_mem_buffer_1_read_data_1_14), .out_8(mem_wb_buffer_1_out_8), .out_9(mem_wb_buffer_1_out_9),
    .out_10(mem_wb_buffer_1_out_10), .out_11(mem_wb_buffer_1_out_11), .out_12(mem_wb_buffer_1_out_12),
    .out_13(mem_wb_buffer_1_out_13));
  Multiplexer #(.width(16), .disabled(0), .enable("false")) multiplexer_7 (
    .in0(mem_wb_buffer_1_out_8), .in1(mem_wb_buffer_1_out_9), .out(multiplexer_7_out),
    .sel(mem_wb_buffer_1_out_10));
  Register #(.width(16)) register_1 (
    .D(mem_wb_buffer_1_out_11), .en(mem_wb_buffer_1_out_12), .Q(register_1_q), .clk(clock_1_out));  // open: clr
  Hex_Digit_Display hex_digit_display_1 (.value(register_1_q[15:12]));  // open: dp
  Hex_Digit_Display hex_digit_display_2 (.value(register_1_q[11:8]));  // open: dp
  LED Halt (.in(mem_wb_buffer_1_out_13));
  Hex_Digit_Display hex_digit_display_3 (.value(register_1_q[7:4]));  // open: dp
  Hex_Digit_Display hex_digit_display_4 (.value(register_1_q[3:0]));  // open: dp

  // Notes on the sheet:
  //   contents of rom_1 (hex, n*v repeats v):
  //   280 160a 1914 2b80 f200 f600 f800 fa00 7000
  //   ID/EX Buffer
  //   EX/MEM Buffer
  //   MEM/WB Buffer
endmodule

module IF_ID_Buffer (
  input  [15:0] Data_in,
  input  ClockIn,
  input  EN,
  output [15:0] Data_out
);

  Register #(.width(16)) Instruction_Memory (.D(Data_in), .en(EN), .Q(Data_out), .clk(ClockIn));  // open: clr
endmodule

module ID_EX_Buffer (
  input  [7:0] PC_plus_4,
  input  CLK,
  input  [7:0] Immediate,
  input  [15:0] Read_Data_1,
  input  [15:0] Read_Data_2,
  input  [15:0] Read_Data_2_2,
  input  [15:0] Sign_Extended_Immediate,
  input  SubOP,
  input  [15:0] Read_Data_1_2,
  input  [15:0] Read_Data_2_3,
  input  ShiftSource,
  input  [3:0] ShiftAmount,
  input  [7:0] PC_Plus_4_2,
  input  Shifter_to_reg,
  input  [3:0] ALU_op,
  input  IMMtoALU,
  input  Reg_to_PC,
  input  IMMtoPC,
  input  Zeros_to_ALU,
  input  MemWrite,
  input  Mem_to_Reg,
  input  LED,
  input  Write_LED,
  input  MemRead,
  input  PC_to_Reg,
  output [7:0] PC_plus_4_3,
  output [7:0] Immediate_2,
  output [15:0] Read_Data_1_3,
  output [15:0] Read_Data_2_4,
  output [15:0] Read_Data_2_5,
  output [15:0] Sign_Extended_Immediate_2,
  output SubOp_2,
  output [15:0] Read_Data_1_4,
  output [15:0] Read_Data_2_6,
  output ShiftSource_2,
  output [3:0] ShiftAmount_2,
  output [7:0] PC_Plus_4_4,
  output Shifter_to_reg_2,
  output [3:0] ALU_op_2,
  output IMMtoALU_2,
  output Reg_to_PC_2,
  output IMMtoPC_2,
  output Zeros_to_ALU_2,
  output MemWrite_2,
  output Mem_to_Reg_2,
  output LED_2,
  output Write_LED_2,
  output MemRead_2,
  output PC_to_Reg_2
);

  Register register_1 (.D(PC_plus_4), .Q(PC_plus_4_3), .clk(CLK));  // open: en, clr
  Register register_2 (.D(Immediate), .Q(Immediate_2), .clk(CLK));  // open: en, clr
  Register #(.width(16)) register_3 (.D(Read_Data_1), .Q(Read_Data_1_3), .clk(CLK));  // open: en, clr
  Register #(.width(16)) register_4 (.D(Read_Data_2), .Q(Read_Data_2_4), .clk(CLK));  // open: en, clr
  Register #(.width(16)) register_5 (.D(Read_Data_2_2), .Q(Read_Data_2_5), .clk(CLK));  // open: en, clr
  Register #(.width(16)) register_6 (
    .D(Sign_Extended_Immediate), .Q(Sign_Extended_Immediate_2), .clk(CLK));  // open: en, clr
  Register #(.width(1)) register_7 (.D(SubOP), .Q(SubOp_2), .clk(CLK));  // open: en, clr
  Register #(.width(16)) register_8 (.D(Read_Data_1_2), .Q(Read_Data_1_4), .clk(CLK));  // open: en, clr
  Register #(.width(16)) register_9 (.D(Read_Data_2_3), .Q(Read_Data_2_6), .clk(CLK));  // open: en, clr
  Register #(.width(1)) register_10 (.D(ShiftSource), .Q(ShiftSource_2), .clk(CLK));  // open: en, clr
  Register #(.width(4)) register_11 (.D(ShiftAmount), .Q(ShiftAmount_2), .clk(CLK));  // open: en, clr
  Register register_12 (.D(PC_Plus_4_2), .Q(PC_Plus_4_4), .clk(CLK));  // open: en, clr
  Register #(.width(1)) register_13 (.D(Shifter_to_reg), .Q(Shifter_to_reg_2), .clk(CLK));  // open: en, clr
  Register #(.width(4)) register_14 (.D(ALU_op), .Q(ALU_op_2), .clk(CLK));  // open: en, clr
  Register #(.width(1)) register_15 (.D(IMMtoALU), .Q(IMMtoALU_2), .clk(CLK));  // open: en, clr
  Register #(.width(1)) register_16 (.D(Reg_to_PC), .Q(Reg_to_PC_2), .clk(CLK));  // open: en, clr
  Register #(.width(1)) register_17 (.D(IMMtoPC), .Q(IMMtoPC_2), .clk(CLK));  // open: en, clr
  Register #(.width(1)) register_18 (.D(Zeros_to_ALU), .Q(Zeros_to_ALU_2), .clk(CLK));  // open: en, clr
  Register #(.width(1)) register_19 (.D(MemWrite), .Q(MemWrite_2), .clk(CLK));  // open: en, clr
  Register #(.width(1)) register_20 (.D(Mem_to_Reg), .Q(Mem_to_Reg_2), .clk(CLK));  // open: en, clr
  Register #(.width(1)) register_21 (.D(LED), .Q(LED_2), .clk(CLK));  // open: en, clr
  Register #(.width(1)) register_22 (.D(Write_LED), .Q(Write_LED_2), .clk(CLK));  // open: en, clr
  Register #(.width(1)) register_23 (.D(MemRead), .Q(MemRead_2), .clk(CLK));  // open: en, clr
  Register #(.width(1)) register_24 (.D(PC_to_Reg), .Q(PC_to_Reg_2), .clk(CLK));  // open: en, clr
endmodule

module EX_MEM_Buffer (
  input  CLK,
  input  [7:0] in_2,
  input  [7:0] in_3,
  input  [15:0] in_4,
  input  [15:0] in_5,
  input  in_6,
  input  [15:0] in_7,
  input  in_8,
  input  [15:0] in_9,
  input  in_10,
  input  [3:0] in_11,
  input  [7:0] in_12,
  input  in_13,
  input  in_14,
  input  in_15,
  input  in_16,
  input  in_17,
  input  in_18,
  input  in_19,
  input  [15:0] in_20,
  output [7:0] out_21,
  output [7:0] Read_Data_1,
  output [15:0] Read_Data_1_2,
  output [15:0] Read_Data_1_3,
  output Read_Data_1_4,
  output [15:0] Read_Data_1_5,
  output Read_Data_1_6,
  output [15:0] Read_Data_1_7,
  output Read_Data_1_8,
  output [3:0] Read_Data_1_9,
  output [7:0] Read_Data_1_10,
  output Read_Data_1_11,
  output Read_Data_1_12,
  output Read_Data_1_13,
  output Read_Data_1_14,
  output Read_Data_1_15,
  output Read_Data_1_16,
  output Read_Data_1_17,
  output [15:0] Read_Data_1_18
);

  Register register_1 (.D(in_2), .Q(out_21), .clk(CLK));  // open: en, clr
  Register register_2 (.D(in_3), .Q(Read_Data_1), .clk(CLK));  // open: en, clr
  Register #(.width(16)) register_3 (.D(in_4), .Q(Read_Data_1_2), .clk(CLK));  // open: en, clr
  Register #(.width(16)) register_4 (.D(in_5), .Q(Read_Data_1_3), .clk(CLK));  // open: en, clr
  Register #(.width(1)) register_5 (.D(in_6), .Q(Read_Data_1_4), .clk(CLK));  // open: en, clr
  Register #(.width(16)) register_6 (.D(in_7), .Q(Read_Data_1_5), .clk(CLK));  // open: en, clr
  Register #(.width(1)) register_7 (.D(in_8), .Q(Read_Data_1_6), .clk(CLK));  // open: en, clr
  Register #(.width(16)) register_8 (.D(in_9), .Q(Read_Data_1_7), .clk(CLK));  // open: en, clr
  Register #(.width(1)) register_9 (.D(in_10), .Q(Read_Data_1_8), .clk(CLK));  // open: en, clr
  Register #(.width(4)) register_10 (.D(in_11), .Q(Read_Data_1_9), .clk(CLK));  // open: en, clr
  Register register_11 (.D(in_12), .Q(Read_Data_1_10), .clk(CLK));  // open: en, clr
  Register #(.width(1)) register_12 (.D(in_13), .Q(Read_Data_1_11), .clk(CLK));  // open: en, clr
  Register #(.width(1)) register_13 (.D(in_14), .Q(Read_Data_1_12), .clk(CLK));  // open: en, clr
  Register #(.width(1)) register_14 (.D(in_15), .Q(Read_Data_1_13), .clk(CLK));  // open: en, clr
  Register #(.width(1)) register_15 (.D(in_16), .Q(Read_Data_1_14), .clk(CLK));  // open: en, clr
  Register #(.width(1)) register_16 (.D(in_17), .Q(Read_Data_1_15), .clk(CLK));  // open: en, clr
  Register #(.width(1)) register_17 (.D(in_18), .Q(Read_Data_1_16), .clk(CLK));  // open: en, clr
  Register #(.width(1)) register_18 (.D(in_19), .en(in_19), .Q(Read_Data_1_17), .clk(CLK));  // open: clr
  Register #(.width(16)) register_19 (.D(in_20), .Q(Read_Data_1_18), .clk(CLK));  // open: en, clr
endmodule

module MEM_WB_Buffer (
  input  CLK,
  input  [15:0] in_2,
  input  [15:0] in_3,
  input  in_4,
  input  [15:0] in_5,
  input  in_6,
  input  in_7,
  output [15:0] out_8,
  output [15:0] out_9,
  output out_10,
  output [15:0] out_11,
  output out_12,
  output out_13
);

  Register #(.width(16)) register_1 (.D(in_2), .Q(out_8), .clk(CLK));  // open: en, clr
  Register #(.width(16)) register_2 (.D(in_3), .Q(out_9), .clk(CLK));  // open: en, clr
  Register #(.width(1)) register_3 (.D(in_4), .Q(out_10), .clk(CLK));  // open: en, clr
  Register #(.width(16)) register_4 (.D(in_5), .Q(out_11), .clk(CLK));  // open: en, clr
  Register #(.width(1)) register_5 (.D(in_6), .Q(out_12), .clk(CLK));  // open: en, clr
  Register #(.width(1)) register_6 (.D(in_7), .Q(out_13), .clk(CLK));  // open: en, clr
endmodule
